// Logisim project snakegame.circ as structural Verilog: 13 circuits, main circuit main
module main (
);

  wire alu_control_1_jr, alu_control_1_sll, alu_control_1_slt, beq_bne_1_out_5, CLK, down, left, or_1_out,
       or_2_out, read_mem, right, uc_w_1_alusrc, uc_w_1_andi, uc_w_1_beq, uc_w_1_bne, uc_w_1_branch,
       uc_w_1_clear, uc_w_1_jal, uc_w_1_jump, uc_w_1_li, uc_w_1_lui, uc_w_1_move, uc_w_1_regdest,
       uc_w_1_regwrite, ula_1_igual, ula_1_menor, up, wr_mem;
  wire [2:0] uc_w_1_aluop;
  wire [4:0] multiplexer_1_out, multiplexer_2_out, multiplexer_3_out, multiplexer_4_out;
  wire [5:0] alu_control_1_out_4;
  wire [15:0] address_in, system_1_out_11, system_1_out_12, system_1_out_13, system_1_out_14,
       system_1_out_16, system_1_out_17, system_1_out_18, system_1_out_19, system_1_out_20, system_1_out_21,
       system_1_out_22, system_1_out_23, system_1_out_24, system_1_out_25, system_1_out_26, system_1_out_27;
  wire [31:0] adder_1_out, adder_2_out, atlas_extensor_1_out_2, atlas_extensor_1_out_3,
       banco_registradores_1_r1, data_mem, DATA_MEMORY_data, data_out, data_write, INSTRUCTION_MEMORY_data,
       multiplexer_5_out, multiplexer_6_out, multiplexer_7_out, multiplexer_8_out, multiplexer_9_out,
       multiplexer_10_out, multiplexer_11_out, multiplexer_12_out, mux_s_1_out_8, PC_q, shifter_1_out,
       ula_1_resultado;

  Register #(.width(32), .Select("low")) PC (.D(mux_s_1_out_8), .Q(PC_q), .clk(CLK));  // open: en, clr
  Adder #(.width(32)) adder_1 (.a(32'h4), .b(PC_q), .out(adder_1_out));  // open: cin, cout
  Clock clock_1 (.out(CLK));
  Adder #(.width(32)) adder_2 (.a(32'h1), .b(PC_q), .out(adder_2_out));  // open: cin, cout
  RAM #(.addrWidth(16), .dataWidth(32), .Select("high"), .simpleMode("false")) INSTRUCTION_MEMORY (
    .addr(PC_q[17:2]), .data(INSTRUCTION_MEMORY_data), .clk(CLK));  // open: sel, ld, clr
  Multiplexer #(.width(5), .enable("false")) multiplexer_1 (
    .in0(INSTRUCTION_MEMORY_data[20:16]), .in1(INSTRUCTION_MEMORY_data[15:11]), .out(multiplexer_1_out),
    .sel(uc_w_1_regdest));
  Multiplexer #(.width(5), .enable("false")) multiplexer_2 (
    .in0(INSTRUCTION_MEMORY_data[25:21]), .in1({5{1'b0}}), .out(multiplexer_2_out), .sel(or_2_out));
  Multiplexer #(.width(5), .enable("false")) multiplexer_3 (
    .in0(INSTRUCTION_MEMORY_data[20:16]), .in1({5{1'b0}}), .out(multiplexer_3_out), .sel(or_1_out));
  Multiplexer #(.width(5), .enable("false")) multiplexer_4 (
    .in0(multiplexer_1_out), .in1({5{1'b1}}), .out(multiplexer_4_out), .sel(uc_w_1_jal));
  or or_1 (or_1_out, uc_w_1_move, uc_w_1_clear);
  or or_2 (or_2_out, uc_w_1_clear, uc_w_1_li);
  UC_W uc_w_1 (
    .in_1(INSTRUCTION_MEMORY_data[31:26]), .REGDEST(uc_w_1_regdest), .JUMP(uc_w_1_jump),
    .BRANCH(uc_w_1_branch), .MEMTOREG(read_mem), .ALUOP(uc_w_1_aluop), .MEMWRITE(wr_mem),
    .ALUSRC(uc_w_1_alusrc), .REGWRITE(uc_w_1_regwrite), .BEQ(uc_w_1_beq), .BNE(uc_w_1_bne), .JAL(uc_w_1_jal),
    .LUI(uc_w_1_lui), .ANDI(uc_w_1_andi), .MOVE(uc_w_1_move), .CLEAR(uc_w_1_clear), .LI(uc_w_1_li));
  Multiplexer #(.width(32), .enable("false")) multiplexer_5 (
    .in0(multiplexer_6_out), .in1({INSTRUCTION_MEMORY_data[15:0], {16{1'b0}}}), .out(multiplexer_5_out),
    .sel(uc_w_1_lui));
  Multiplexer #(.width(32), .enable("false")) multiplexer_6 (
    .in0(multiplexer_7_out), .in1(adder_2_out), .out(multiplexer_6_out), .sel(uc_w_1_jal));
  Multiplexer #(.width(32), .enable("false")) multiplexer_7 (
    .in0(multiplexer_8_out), .in1(shifter_1_out), .out(multiplexer_7_out), .sel(alu_control_1_sll));
  Multiplexer #(.width(32), .enable("false")) multiplexer_8 (
    .in0(data_out), .in1(multiplexer_9_out), .out(multiplexer_8_out), .sel(alu_control_1_slt));
  Multiplexer #(.width(32), .enable("false")) multiplexer_9 (
    .in0({32{1'b0}}), .in1(32'h1), .out(multiplexer_9_out), .sel(ula_1_menor));
  banco_registradores banco_registradores_1 (
    .R1_num(multiplexer_2_out), .R2_num(multiplexer_3_out), .RW(multiplexer_4_out), .Din(multiplexer_5_out),
    .WE(uc_w_1_regwrite), .clk(CLK), .R1(banco_registradores_1_r1), .R2(data_write));
  SYSTEM system_1 (
    .DATA_OUT(data_out), .ADDRESS_IN(address_in), .wr_mem(wr_mem), .DATA_WR(data_write), .LEFT(right),
    .DOWN(down), .RIGHT(left), .UP(up), .DATA_MEM(data_mem), .CLK(CLK), .MEM_READ(read_mem),
    .out_11(system_1_out_11), .out_12(system_1_out_12), .out_13(system_1_out_13), .out_14(system_1_out_14),
    .out_16(system_1_out_16), .out_17(system_1_out_17), .out_18(system_1_out_18), .out_19(system_1_out_19),
    .out_20(system_1_out_20), .out_21(system_1_out_21), .out_22(system_1_out_22), .out_23(system_1_out_23),
    .out_24(system_1_out_24), .out_25(system_1_out_25), .out_26(system_1_out_26), .out_27(system_1_out_27));
  DotMatrix #(.inputtype("row"), .matrixcols(16), .matrixrows(16)) dotmatrix_1 (
    .row0(system_1_out_11), .row1(system_1_out_12), .row2(system_1_out_13), .row3(system_1_out_14),
    .row4(system_1_out_16), .row5(system_1_out_17), .row6(system_1_out_18), .row7(system_1_out_19),
    .row8(system_1_out_20), .row9(system_1_out_21), .row10(system_1_out_22), .row11(system_1_out_23),
    .row12(system_1_out_24), .row13(system_1_out_25), .row14(system_1_out_26), .row15(system_1_out_27));
  Shifter #(.width(32)) shifter_1 (.in(data_write), .\dist (INSTRUCTION_MEMORY_data[10:6]), .out(shifter_1_out));
  Button button_1 (.out(left));
  Multiplexer #(.width(32), .enable("false")) multiplexer_10 (
    .in0(atlas_extensor_1_out_3), .in1(atlas_extensor_1_out_2), .out(multiplexer_10_out), .sel(uc_w_1_andi));
  atlas_extensor atlas_extensor_1 (
    .in_1(INSTRUCTION_MEMORY_data[15:0]), .out_2(atlas_extensor_1_out_2), .out_3(atlas_extensor_1_out_3));
  ALU_CONTROL alu_control_1 (
    .in_1(INSTRUCTION_MEMORY_data[5:0]), .out_4(alu_control_1_out_4), .in_2(uc_w_1_aluop),
    .SLT(alu_control_1_slt), .JR(alu_control_1_jr), .SLL(alu_control_1_sll));
  Button button_2 (.out(up));
  Button button_3 (.out(right));
  Button button_4 (.out(down));
  Multiplexer #(.width(32), .enable("false")) multiplexer_11 (
    .in0(banco_registradores_1_r1), .in1({32{1'b0}}), .out(multiplexer_11_out), .sel(alu_control_1_jr));
  ULA ula_1 (
    .A(multiplexer_11_out), .B(multiplexer_12_out), .Resultado(ula_1_resultado), .OP(alu_control_1_out_4),
    .igual(ula_1_igual), .menor(ula_1_menor));
  Multiplexer #(.width(32), .enable("false")) multiplexer_12 (
    .in0(data_write), .in1(multiplexer_10_out), .out(multiplexer_12_out), .sel(uc_w_1_alusrc));
  BEQ_BNE beq_bne_1 (
    .BRANCH(uc_w_1_branch), .BEQ(uc_w_1_beq), .BNE(uc_w_1_bne), .out_5(beq_bne_1_out_5), .in_4(ula_1_igual));
  Bit_Extender #(.in_width(32), .\type ("zero")) bit_extender_1 (.in(ula_1_resultado), .out(address_in));
  MUX_S mux_s_1 (
    .PC___4(adder_1_out), .IMEDIATO_EXT(atlas_extensor_1_out_3), .RD(banco_registradores_1_r1),
    .JUMP(uc_w_1_jump), .BEQ_BNE(beq_bne_1_out_5), .JAL(uc_w_1_jal), .JR(alu_control_1_jr),
    .out_8(mux_s_1_out_8));
  RAM #(.addrWidth(16), .dataWidth(32), .bus("separate"), .Select("high"), .simpleMode("false")) DATA_MEMORY (
    .addr(address_in), .din(data_write), .data(DATA_MEMORY_data), .str(wr_mem), .clk(CLK));  // open: sel, ld, clr
  Multiplexer #(.width(32), .enable("false")) multiplexer_13 (
    .in0(ula_1_resultado), .in1(DATA_MEMORY_data), .out(data_mem), .sel(read_mem));

  // Notes on the sheet:
  //   RegDest
  //   MOVE
  //   CLEAR
  //   LI
  //   Jump
  //   Branch
  //   MenToReg
  //   ALUOp
  //   MemWrite
  //   AluSRC
  //   RegWrite
endmodule

module banco_registradores (
  input  [4:0] R1_num,
  input  [4:0] R2_num,
  input  [4:0] RW,
  input  [31:0] Din,
  input  WE,
  input  clk,
  output [31:0] R1,
  output [31:0] R2
);

  wire demultiplexer_1_out0, demultiplexer_1_out1, demultiplexer_1_out2, demultiplexer_1_out3,
       demultiplexer_2_out0, demultiplexer_2_out1, demultiplexer_2_out2, demultiplexer_2_out3,
       demultiplexer_2_out4, demultiplexer_2_out5, demultiplexer_2_out6, demultiplexer_2_out7,
       demultiplexer_3_out0, demultiplexer_3_out1, demultiplexer_3_out2, demultiplexer_3_out3,
       demultiplexer_3_out4, demultiplexer_3_out5, demultiplexer_3_out6, demultiplexer_3_out7,
       demultiplexer_4_out0, demultiplexer_4_out1, demultiplexer_4_out2, demultiplexer_4_out3,
       demultiplexer_4_out4, demultiplexer_4_out5, demultiplexer_4_out6, demultiplexer_4_out7,
       demultiplexer_5_out0, demultiplexer_5_out1, demultiplexer_5_out2, demultiplexer_5_out3,
       demultiplexer_5_out4, demultiplexer_5_out5, demultiplexer_5_out6, demultiplexer_5_out7;
  wire [31:0] _0__Zero_q, _1__at_q, _3__v1_q, _5__a1_q, _6__a2_q, _7__a3_q, _8__t0_q, _9__t1_q, _10__t2_q,
       _11__t3_q, _12__t4_q, _13__t5_q, _14__t6_q, _15__t7_q, _19__s3_q, _20__s4_q, _21__s5_q, _22__s6_q,
       _23__s7_q, _24__t8_q, _25__t9_q, _26__k0_q, _27__k1_q, _28__gp_q, _29__sp_q, _30__fp_q, a0, ra, s0,
       s1, s2, v0;

  Demultiplexer #(.select(2), .disabled(0)) demultiplexer_1 (
    .out0(demultiplexer_1_out0), .out1(demultiplexer_1_out1), .out2(demultiplexer_1_out2),
    .out3(demultiplexer_1_out3), .in(1'b1), .sel(RW[4:3]), .en(WE));
  Demultiplexer #(.select(3), .disabled(0)) demultiplexer_2 (
    .out0(demultiplexer_2_out0), .out1(demultiplexer_2_out1), .out2(demultiplexer_2_out2),
    .out3(demultiplexer_2_out3), .out4(demultiplexer_2_out4), .out5(demultiplexer_2_out5),
    .out6(demultiplexer_2_out6), .out7(demultiplexer_2_out7), .in(1'b1), .sel(RW[2:0]),
    .en(demultiplexer_1_out0));
  Demultiplexer #(.select(3), .disabled(0)) demultiplexer_3 (
    .out0(demultiplexer_3_out0), .out1(demultiplexer_3_out1), .out2(demultiplexer_3_out2),
    .out3(demultiplexer_3_out3), .out4(demultiplexer_3_out4), .out5(demultiplexer_3_out5),
    .out6(demultiplexer_3_out6), .out7(demultiplexer_3_out7), .in(1'b1), .sel(RW[2:0]),
    .en(demultiplexer_1_out1));
  Demultiplexer #(.select(3), .disabled(0)) demultiplexer_4 (
    .out0(demultiplexer_4_out0), .out1(demultiplexer_4_out1), .out2(demultiplexer_4_out2),
    .out3(demultiplexer_4_out3), .out4(demultiplexer_4_out4), .out5(demultiplexer_4_out5),
    .out6(demultiplexer_4_out6), .out7(demultiplexer_4_out7), .in(1'b1), .sel(RW[2:0]),
    .en(demultiplexer_1_out2));
  Demultiplexer #(.select(3), .disabled(0)) demultiplexer_5 (
    .out0(demultiplexer_5_out0), .out1(demultiplexer_5_out1), .out2(demultiplexer_5_out2),
    .out3(demultiplexer_5_out3), .out4(demultiplexer_5_out4), .out5(demultiplexer_5_out5),
    .out6(demultiplexer_5_out6), .out7(demultiplexer_5_out7), .in(1'b1), .sel(RW[2:0]),
    .en(demultiplexer_1_out3));
  Register #(.width(32), .Select("low")) _0__Zero (
    .D(Din), .en(demultiplexer_2_out0), .Q(_0__Zero_q));  // open: clk, clr
  Register #(.width(32), .Select("low")) _8__t0 (
    .D(Din), .en(demultiplexer_3_out0), .Q(_8__t0_q), .clk(clk));  // open: clr
  Register #(.width(32), .Select("low")) _16__s0 (.D(Din), .en(demultiplexer_4_out0), .Q(s0), .clk(clk));  // open: clr
  Register #(.width(32), .Select("low")) _24__t8 (
    .D(Din), .en(demultiplexer_5_out0), .Q(_24__t8_q), .clk(clk));  // open: clr
  Register #(.width(32), .Select("low")) _1__at (
    .D(Din), .en(demultiplexer_2_out1), .Q(_1__at_q), .clk(clk));  // open: clr
  Register #(.width(32), .Select("low")) _9__t1 (
    .D(Din), .en(demultiplexer_3_out1), .Q(_9__t1_q), .clk(clk));  // open: clr
  Register #(.width(32), .Select("low")) _17__s1 (.D(Din), .en(demultiplexer_4_out1), .Q(s1), .clk(clk));  // open: clr
  Register #(.width(32), .Select("low")) _25__t9 (
    .D(Din), .en(demultiplexer_5_out1), .Q(_25__t9_q), .clk(clk));  // open: clr
  Register #(.width(32), .Select("low")) _2__v0 (.D(Din), .en(demultiplexer_2_out2), .Q(v0), .clk(clk));  // open: clr
  Register #(.width(32), .Select("low")) _10__t2 (
    .D(Din), .en(demultiplexer_3_out2), .Q(_10__t2_q), .clk(clk));  // open: clr
  Register #(.width(32), .Select("low")) _18__s2 (.D(Din), .en(demultiplexer_4_out2), .Q(s2), .clk(clk));  // open: clr
  Register #(.width(32), .Select("low")) _26__k0 (
    .D(Din), .en(demultiplexer_5_out2), .Q(_26__k0_q), .clk(clk));  // open: clr
  Register #(.width(32), .Select("low")) _3__v1 (
    .D(Din), .en(demultiplexer_2_out3), .Q(_3__v1_q), .clk(clk));  // open: clr
  Register #(.width(32), .Select("low")) _11__t3 (
    .D(Din), .en(demultiplexer_3_out3), .Q(_11__t3_q), .clk(clk));  // open: clr
  Register #(.width(32), .Select("low")) _19__s3 (
    .D(Din), .en(demultiplexer_4_out3), .Q(_19__s3_q), .clk(clk));  // open: clr
  Register #(.width(32), .Select("low")) _27__k1 (
    .D(Din), .en(demultiplexer_5_out3), .Q(_27__k1_q), .clk(clk));  // open: clr
  Register #(.width(32), .Select("low")) _4__a0 (.D(Din), .en(demultiplexer_2_out4), .Q(a0), .clk(clk));  // open: clr
  Register #(.width(32), .Select("low")) _12__t4 (
    .D(Din), .en(demultiplexer_3_out4), .Q(_12__t4_q), .clk(clk));  // open: clr
  Register #(.width(32), .Select("low")) _20__s4 (
    .D(Din), .en(demultiplexer_4_out4), .Q(_20__s4_q), .clk(clk));  // open: clr
  Register #(.width(32), .Select("low")) _28__gp (
    .D(Din), .en(demultiplexer_5_out4), .Q(_28__gp_q), .clk(clk));  // open: clr
  Register #(.width(32), .Select("low")) _5__a1 (
    .D(Din), .en(demultiplexer_2_out5), .Q(_5__a1_q), .clk(clk));  // open: clr
  Register #(.width(32), .Select("low")) _13__t5 (
    .D(Din), .en(demultiplexer_3_out5), .Q(_13__t5_q), .clk(clk));  // open: clr
  Register #(.width(32), .Select("low")) _21__s5 (
    .D(Din), .en(demultiplexer_4_out5), .Q(_21__s5_q), .clk(clk));  // open: clr
  Register #(.width(32), .Select("low")) _29__sp (
    .D(Din), .en(demultiplexer_5_out5), .Q(_29__sp_q), .clk(clk));  // open: clr
  Register #(.width(32), .Select("low")) _6__a2 (
    .D(Din), .en(demultiplexer_2_out6), .Q(_6__a2_q), .clk(clk));  // open: clr
  Register #(.width(32), .Select("low")) _14__t6 (
    .D(Din), .en(demultiplexer_3_out6), .Q(_14__t6_q), .clk(clk));  // open: clr
  Register #(.width(32), .Select("low")) _22__s6 (
    .D(Din), .en(demultiplexer_4_out6), .Q(_22__s6_q), .clk(clk));  // open: clr
  Register #(.width(32), .Select("low")) _30__fp (
    .D(Din), .en(demultiplexer_5_out6), .Q(_30__fp_q), .clk(clk));  // open: clr
  Register #(.width(32), .Select("low")) _7__a3 (
    .D(Din), .en(demultiplexer_2_out7), .Q(_7__a3_q), .clk(clk));  // open: clr
  Register #(.width(32), .Select("low")) _15__t7 (
    .D(Din), .en(demultiplexer_3_out7), .Q(_15__t7_q), .clk(clk));  // open: clr
  Register #(.width(32), .Select("low")) _23__s7 (
    .D(Din), .en(demultiplexer_4_out7), .Q(_23__s7_q), .clk(clk));  // open: clr
  Register #(.width(32), .Select("low")) _31__ra (.D(Din), .en(demultiplexer_5_out7), .Q(ra), .clk(clk));  // open: clr
  Multiplexer #(.select(5), .width(32), .enable("false")) multiplexer_1 (
    .in0(_0__Zero_q), .in1(_1__at_q), .in2(v0), .in3(_3__v1_q), .in4(a0), .in5(_5__a1_q), .in6(_6__a2_q),
    .in7(_7__a3_q), .in8(_8__t0_q), .in9(_9__t1_q), .in10(_10__t2_q), .in11(_11__t3_q), .in12(_12__t4_q),
    .in13(_13__t5_q), .in14(_14__t6_q), .in15(_15__t7_q), .in16(s0), .in17(s1), .in18(s2), .in19(_19__s3_q),
    .in20(_20__s4_q), .in21(_21__s5_q), .in22(_22__s6_q), .in23(_23__s7_q), .in24(_24__t8_q),
    .in25(_25__t9_q), .in26(_26__k0_q), .in27(_27__k1_q), .in28(_28__gp_q), .in29(_29__sp_q),
    .in30(_30__fp_q), .in31(ra), .out(R1), .sel(R1_num));
  Multiplexer #(.select(5), .width(32), .enable("false")) multiplexer_2 (
    .in0(_0__Zero_q), .in1(_1__at_q), .in2(v0), .in3(_3__v1_q), .in4(a0), .in5(_5__a1_q), .in6(_6__a2_q),
    .in7(_7__a3_q), .in8(_8__t0_q), .in9(_9__t1_q), .in10(_10__t2_q), .in11(_11__t3_q), .in12(_12__t4_q),
    .in13(_13__t5_q), .in14(_14__t6_q), .in15(_15__t7_q), .in16(s0), .in17(s1), .in18(s2), .in19(_19__s3_q),
    .in20(_20__s4_q), .in21(_21__s5_q), .in22(_22__s6_q), .in23(_23__s7_q), .in24(_24__t8_q),
    .in25(_25__t9_q), .in26(_26__k0_q), .in27(_27__k1_q), .in28(_28__gp_q), .in29(_29__sp_q),
    .in30(_30__fp_q), .in31(ra), .out(R2), .sel(R2_num));

  // Other names for the same wires on the sheet: reg1[31:0] = R1; reg1_num[4:0] = R1_num; reg2[31:0] = R2;
  //   reg2_num[4:0] = R2_num; write_data[31:0] = Din; write_reg_num[4:0] = RW

  // Notes on the sheet:
  //   Input
  //   Output
endmodule

module ULA (
  input  [31:0] A,
  input  [31:0] B,
  input  [5:0] OP,
  output igual,
  output menor,
  output [31:0] Resultado
);

  wire [31:0] adder_1_out, and_1_out, divider_1_out, multiplier_1_out, subtractor_1_out;

  assign and_1_out = A & B;  // AND_Gate and_1, 32 bits wide
  Adder #(.width(32)) adder_1 (.a(A), .b(B), .out(adder_1_out));  // open: cin, cout
  Subtractor #(.width(32)) subtractor_1 (.a(A), .b(B), .out(subtractor_1_out));  // open: bin, bout
  Multiplier #(.width(32)) multiplier_1 (.a(A), .b(B), .out(multiplier_1_out));  // open: cin, cout
  Divider #(.width(32)) divider_1 (.a(A), .b(B), .out(divider_1_out));  // open: upper, rem
  Comparator #(.width(32)) comparator_1 (.a(A), .b(B), .eq(igual), .lt(menor));  // open: gt
  Multiplexer #(.select(4), .width(32), .enable("false")) multiplexer_1 (
    .in0(adder_1_out), .in1(subtractor_1_out), .in2(multiplier_1_out), .in3(divider_1_out), .in12(and_1_out),
    .out(Resultado), .sel(OP[3:0]));  // open: in4, in5, in6, in7, in8, in9, in10, in11, in13, in14, in15
endmodule

module UC (
  input  UC5,
  input  UC4,
  input  UC3,
  input  UC2,
  input  UC1,
  input  UC0,
  output REGDEST,
  output JUMP,
  output BRANCH,
  output MEMTOREG,
  output ULA0P1,
  output ULA0P0,
  output ULAOPSRC,
  output MEM_WR,
  output ULASRC,
  output WR,
  output BEQ,
  output BNE,
  output JAL,
  output LUI,
  output ANDI,
  output MOVE,
  output CLEAR,
  output LI
);

  wire and_1_out, and_2_out, and_3_out, and_4_out, and_5_out, and_6_out, and_7_out, and_8_out, and_9_out,
       and_10_out, and_11_out, and_12_out, and_13_out, and_14_out, and_15_out, and_16_out, and_17_out,
       and_18_out, and_19_out, and_20_out, and_21_out, and_22_out, and_23_out, and_24_out, and_25_out,
       and_26_out, and_27_out, and_28_out, and_29_out, and_30_out, and_31_out, and_32_out, and_33_out,
       and_34_out, and_35_out, and_36_out, and_37_out, and_38_out, and_39_out, and_40_out, and_41_out,
       and_42_out, and_43_out, and_44_out, and_45_out, and_46_out, and_47_out, and_48_out, and_49_out,
       and_50_out, and_51_out, and_52_out, and_53_out, and_54_out, and_55_out, and_56_out, and_57_out,
       and_58_out, and_59_out, and_60_out, and_64_out, and_65_out, not_1_out, not_2_out, not_3_out,
       not_4_out, not_5_out, not_6_out, not_7_out, not_8_out, not_9_out, not_10_out, not_11_out, not_12_out,
       not_13_out, not_14_out, not_15_out, not_16_out, not_17_out, not_18_out, not_19_out, not_20_out,
       not_21_out, not_22_out, not_23_out, not_24_out, not_25_out, not_26_out, not_27_out, not_28_out,
       not_29_out, not_30_out, not_31_out, not_32_out, not_33_out, not_34_out, not_35_out, not_36_out,
       not_37_out, not_38_out, not_39_out, not_40_out, not_41_out, not_42_out, not_43_out, not_44_out,
       not_45_out, not_46_out, not_47_out, not_48_out, not_49_out, not_50_out, not_51_out, not_52_out,
       not_53_out, not_54_out, not_55_out, not_56_out, not_57_out, not_58_out, not_59_out, not_60_out,
       not_61_out, not_62_out, not_63_out, not_64_out, not_65_out, not_66_out, not_67_out, not_68_out,
       not_69_out, not_70_out, not_71_out, not_72_out, not_73_out, not_74_out, not_75_out, not_76_out,
       not_77_out, not_78_out, not_79_out, not_80_out, not_81_out, not_82_out, not_83_out, not_84_out,
       not_85_out, not_86_out, not_87_out, not_88_out, not_89_out, not_90_out, not_91_out, not_92_out,
       not_93_out, not_94_out, not_95_out, not_96_out, not_97_out, not_98_out, not_99_out, not_100_out,
       not_101_out, not_102_out, not_103_out, not_104_out, not_105_out, not_106_out, not_107_out,
       not_108_out, not_109_out, not_110_out, not_111_out, not_112_out, not_113_out, not_114_out,
       not_115_out, not_116_out, not_117_out, not_118_out, not_119_out, not_120_out, not_121_out,
       not_122_out, not_123_out, not_124_out, not_125_out;

  not not_1 (not_1_out, UC2);
  not not_2 (not_2_out, UC1);
  not not_3 (not_3_out, UC0);
  not not_4 (not_4_out, UC3);
  not not_5 (not_5_out, UC1);
  not not_6 (not_6_out, UC2);
  not not_7 (not_7_out, UC0);
  not not_8 (not_8_out, UC5);
  not not_9 (not_9_out, UC4);
  not not_10 (not_10_out, UC2);
  not not_11 (not_11_out, UC1);
  not not_12 (not_12_out, UC0);
  not not_13 (not_13_out, UC5);
  not not_14 (not_14_out, UC4);
  not not_15 (not_15_out, UC2);
  not not_16 (not_16_out, UC5);
  not not_17 (not_17_out, UC4);
  not not_18 (not_18_out, UC3);
  not not_19 (not_19_out, UC1);
  not not_20 (not_20_out, UC5);
  not not_21 (not_21_out, UC4);
  not not_22 (not_22_out, UC2);
  not not_23 (not_23_out, UC1);
  not not_24 (not_24_out, UC5);
  not not_25 (not_25_out, UC4);
  not not_26 (not_26_out, UC2);
  not not_27 (not_27_out, UC0);
  not not_28 (not_28_out, UC3);
  not not_29 (not_29_out, UC0);
  not not_30 (not_30_out, UC3);
  not not_31 (not_31_out, UC2);
  not not_32 (not_32_out, UC3);
  not not_33 (not_33_out, UC1);
  not not_34 (not_34_out, UC1);
  not not_35 (not_35_out, UC2);
  not not_36 (not_36_out, UC1);
  not not_37 (not_37_out, UC2);
  not not_38 (not_38_out, UC1);
  not not_39 (not_39_out, UC4);
  not not_40 (not_40_out, UC3);
  not not_41 (not_41_out, UC2);
  not not_42 (not_42_out, UC0);
  not not_43 (not_43_out, UC3);
  not not_44 (not_44_out, UC1);
  not not_45 (not_45_out, UC1);
  not not_46 (not_46_out, UC0);
  not not_47 (not_47_out, UC0);
  not not_48 (not_48_out, UC0);
  not not_49 (not_49_out, UC0);
  not not_50 (not_50_out, UC1);
  not not_51 (not_51_out, UC3);
  not not_52 (not_52_out, UC3);
  not not_53 (not_53_out, UC2);
  not not_54 (not_54_out, UC3);
  not not_55 (not_55_out, UC1);
  not not_56 (not_56_out, UC0);
  not not_57 (not_57_out, UC2);
  not not_58 (not_58_out, UC1);
  not not_59 (not_59_out, UC0);
  not not_60 (not_60_out, UC5);
  not not_61 (not_61_out, UC4);
  not not_62 (not_62_out, UC3);
  not not_63 (not_63_out, UC1);
  not not_64 (not_64_out, UC0);
  not not_65 (not_65_out, UC3);
  not not_66 (not_66_out, UC2);
  not not_67 (not_67_out, UC3);
  not not_68 (not_68_out, UC0);
  not not_69 (not_69_out, UC1);
  not not_70 (not_70_out, UC5);
  not not_71 (not_71_out, UC4);
  not not_72 (not_72_out, UC3);
  not not_73 (not_73_out, UC2);
  not not_74 (not_74_out, UC5);
  not not_75 (not_75_out, UC4);
  not not_76 (not_76_out, UC3);
  not not_77 (not_77_out, UC0);
  not not_78 (not_78_out, UC5);
  not not_79 (not_79_out, UC3);
  not not_80 (not_80_out, UC2);
  not not_81 (not_81_out, UC1);
  not not_82 (not_82_out, UC5);
  not not_83 (not_83_out, UC3);
  not not_84 (not_84_out, UC2);
  not not_85 (not_85_out, UC0);
  not not_86 (not_86_out, UC5);
  not not_87 (not_87_out, UC4);
  not not_88 (not_88_out, UC1);
  not not_89 (not_89_out, UC0);
  not not_90 (not_90_out, UC5);
  not not_91 (not_91_out, UC4);
  not not_92 (not_92_out, UC5);
  not not_93 (not_93_out, UC4);
  not not_94 (not_94_out, UC2);
  not not_95 (not_95_out, UC1);
  not not_96 (not_96_out, UC5);
  not not_97 (not_97_out, UC4);
  not not_98 (not_98_out, UC2);
  not not_99 (not_99_out, UC0);
  not not_100 (not_100_out, UC5);
  not not_101 (not_101_out, UC4);
  not not_102 (not_102_out, UC2);
  not not_103 (not_103_out, UC5);
  not not_104 (not_104_out, UC4);
  not not_105 (not_105_out, UC5);
  not not_106 (not_106_out, UC3);
  not not_107 (not_107_out, UC2);
  not not_108 (not_108_out, UC1);
  not not_109 (not_109_out, UC5);
  not not_110 (not_110_out, UC4);
  not not_111 (not_111_out, UC1);
  not not_112 (not_112_out, UC0);
  not not_113 (not_113_out, UC5);
  not not_114 (not_114_out, UC3);
  not not_115 (not_115_out, UC2);
  not not_116 (not_116_out, UC1);
  not not_117 (not_117_out, UC0);
  not not_118 (not_118_out, UC5);
  not not_119 (not_119_out, UC3);
  not not_120 (not_120_out, UC2);
  not not_121 (not_121_out, UC1);
  not not_122 (not_122_out, UC5);
  not not_123 (not_123_out, UC3);
  not not_124 (not_124_out, UC2);
  not not_125 (not_125_out, UC0);
  and and_1 (and_1_out, not_1_out, not_2_out, not_3_out);
  and and_2 (and_2_out, not_4_out, UC2, UC0);
  and and_3 (and_3_out, UC2, not_5_out, UC0);
  and and_4 (and_4_out, UC3, not_6_out, UC1, UC0);
  and and_5 (and_5_out, UC3, UC2, UC1, not_7_out);
  and and_6 (and_6_out, UC4, UC0);
  and and_7 (and_7_out, UC4, UC2);
  and and_8 (and_8_out, UC4, UC3);
  and and_9 (and_9_out, not_8_out, not_9_out, UC3, not_10_out, not_11_out, not_12_out);
  and and_10 (and_10_out, not_13_out, not_14_out, UC3, not_15_out, UC1, UC0);
  and and_11 (and_11_out, not_16_out, not_17_out, not_18_out, UC2, not_19_out, UC0);
  and and_12 (and_12_out, not_20_out, not_21_out, UC3, not_22_out, not_23_out, UC0);
  and and_13 (and_13_out, not_24_out, not_25_out, UC3, not_26_out, UC1, not_27_out);
  and and_14 (and_14_out, not_28_out, UC2, UC1);
  and and_15 (and_15_out, UC2, UC1, not_29_out);
  and and_16 (and_16_out, UC4, UC2, UC1);
  and and_17 (and_17_out, UC5, UC2, UC1);
  and and_18 (and_18_out, not_30_out, not_31_out, UC1, UC0);
  and and_19 (and_19_out, not_32_out, UC2, not_33_out);
  and and_20 (and_20_out, UC2, not_34_out, UC0);
  and and_21 (and_21_out, UC4, not_35_out, UC1, UC0);
  and and_22 (and_22_out, UC4, UC2, not_36_out);
  and and_23 (and_23_out, UC5, not_37_out, UC1, UC0);
  and and_24 (and_24_out, UC5, UC2, not_38_out);
  and and_25 (and_25_out, not_39_out, not_40_out, not_41_out, UC1, not_42_out);
  and and_26 (and_26_out, not_43_out, UC2, not_44_out);
  and and_27 (and_27_out, UC2, not_45_out, UC0);
  and and_28 (and_28_out, UC3, UC2, UC1, not_46_out);
  and and_29 (and_29_out, UC4, UC2, not_47_out);
  and and_30 (and_30_out, UC4, UC3, UC1, not_48_out);
  and and_31 (and_31_out, UC5, UC1, not_49_out);
  and and_32 (and_32_out, UC5, UC2, not_50_out);
  and and_33 (and_33_out, not_51_out, UC0);
  and and_34 (and_34_out, not_52_out, UC1);
  and and_35 (and_35_out, not_53_out, UC1, UC0);
  and and_36 (and_36_out, not_54_out, UC2);
  and and_37 (and_37_out, UC2, not_55_out, UC0);
  and and_38 (and_38_out, UC2, UC1, not_56_out);
  and and_39 (and_39_out, UC3, not_57_out, not_58_out, not_59_out);
  and and_40 (and_40_out, UC4, UC3);
  and and_41 (and_41_out, UC5, UC3);
  and and_42 (and_42_out, not_60_out, not_61_out, not_62_out, UC2, UC1, UC0);
  and and_43 (and_43_out, UC3, UC2, not_63_out, UC0);
  and and_44 (and_44_out, UC3, UC2, UC1, not_64_out);
  and and_45 (and_45_out, UC4, UC3);
  and and_46 (and_46_out, UC5, UC3);
  and and_47 (and_47_out, not_65_out, not_66_out, UC0);
  and and_48 (and_48_out, not_67_out, UC1);
  and and_49 (and_49_out, UC2, not_68_out);
  and and_50 (and_50_out, UC3, UC2, not_69_out);
  and and_51 (and_51_out, UC4, UC0);
  and and_52 (and_52_out, UC4, UC1);
  and and_53 (and_53_out, UC5, UC0);
  and and_54 (and_54_out, UC5, UC1);
  and and_55 (and_55_out, not_70_out, not_71_out, not_72_out, not_73_out);
  and and_56 (and_56_out, not_74_out, not_75_out, not_76_out, not_77_out);
  and and_57 (and_57_out, not_78_out, not_79_out, not_80_out, not_81_out);
  and and_58 (and_58_out, not_82_out, not_83_out, not_84_out, not_85_out);
  and and_59 (and_59_out, not_86_out, not_87_out, UC2, not_88_out, not_89_out);
  and and_60 (and_60_out, not_90_out, not_91_out, UC3, UC1, UC0);
  and and_61 (BEQ, not_92_out, not_93_out, UC3, not_94_out, not_95_out, UC0);
  and and_62 (BNE, not_96_out, not_97_out, UC3, not_98_out, UC1, not_99_out);
  and and_63 (JAL, not_100_out, not_101_out, UC3, not_102_out, UC1, UC0);
  and and_64 (and_64_out, not_103_out, not_104_out, UC3, UC2, UC1, UC0);
  and and_65 (and_65_out, not_105_out, UC4, not_106_out, not_107_out, not_108_out, UC0);
  and and_66 (ANDI, not_109_out, not_110_out, UC3, UC2, not_111_out, not_112_out);
  and and_67 (MOVE, not_113_out, UC4, not_114_out, not_115_out, not_116_out, not_117_out);
  and and_68 (CLEAR, not_118_out, UC4, not_119_out, not_120_out, not_121_out, UC0);
  and and_69 (LI, not_122_out, UC4, not_123_out, not_124_out, UC1, not_125_out);
  or or_1 (REGDEST, and_1_out, and_2_out, and_3_out, and_4_out, and_5_out, and_6_out, and_7_out, and_8_out, UC5);
  or or_2 (JUMP, and_9_out, and_10_out);
  or or_3 (BRANCH, and_11_out, and_12_out, and_13_out);
  or or_4 (MEMTOREG, and_14_out, and_15_out, and_16_out, and_17_out);
  or or_5 (ULA0P1, and_18_out, and_19_out, and_20_out, and_21_out, and_22_out, and_23_out, and_24_out);
  or or_6 (ULA0P0, and_25_out, and_26_out, and_27_out, and_28_out, and_29_out, and_30_out, and_31_out, and_32_out);
  or or_7 (ULAOPSRC, and_33_out, and_34_out, and_35_out, and_36_out, and_37_out, and_38_out, and_39_out, and_40_out, and_41_out);
  or or_8 (MEM_WR, and_42_out, and_43_out, and_44_out, and_45_out, and_46_out);
  or or_9 (ULASRC, and_47_out, and_48_out, and_49_out, and_50_out, and_51_out, and_52_out, and_53_out, and_54_out);
  or or_10 (WR, and_55_out, and_56_out, and_57_out, and_58_out, and_59_out, and_60_out);
  or or_11 (LUI, and_64_out, and_65_out);
endmodule

// ULAOP
module OPULA (
  input  OPCOD0,
  input  OPCOD1,
  input  OPCOD2,
  input  OPCOD3,
  input  OPCOD4,
  input  OPCOD5,
  input  FUNC0,
  input  FUNC1,
  input  FUNC2,
  input  FUNC3,
  input  FUNC4,
  input  FUNC5,
  output ULAOP0,
  output ULAOP1,
  output ULAOP2,
  output ULAOP3
);
endmodule

// ALUCONTROL
module ALU_CONTROL (
  input  [5:0] in_1,
  input  [2:0] in_2,
  output SLL,
  output [5:0] out_4,
  output SLT,
  output JR
);

  wire comparator_1_eq, comparator_2_eq, comparator_3_eq, comparator_4_eq, comparator_5_eq, comparator_6_eq;
  wire [5:0] bit_extender_1_out;

  assign bit_extender_1_out = {{4{1'b0}}, in_2[1:0]};  // Bit_Extender bit_extender_1
  Multiplexer #(.width(6), .enable("false")) multiplexer_1 (
    .in0(in_1), .in1(bit_extender_1_out), .out(out_4), .sel(in_2[2]));
  Comparator #(.width(6)) comparator_1 (.a(in_1), .b(6'b000100), .eq(comparator_1_eq));  // open: gt, lt
  Comparator #(.width(3)) comparator_2 (.a(in_2), .b(3'b000), .eq(comparator_2_eq));  // open: gt, lt
  and and_1 (SLT, comparator_1_eq, comparator_2_eq);
  Comparator #(.width(6)) comparator_3 (.a(in_1), .b(6'b000101), .eq(comparator_3_eq));  // open: gt, lt
  Comparator #(.width(3)) comparator_4 (.a(in_2), .b(3'b000), .eq(comparator_4_eq));  // open: gt, lt
  Comparator #(.width(3)) comparator_5 (.a(in_2), .b(3'b000), .eq(comparator_5_eq));  // open: gt, lt
  Comparator #(.width(6)) comparator_6 (.a(in_1), .b(6'b000110), .eq(comparator_6_eq));  // open: gt, lt
  and and_2 (SLL, comparator_6_eq, comparator_5_eq);
  and and_3 (JR, comparator_3_eq, comparator_4_eq);
endmodule

// UC
module UC_W (
  input  [5:0] in_1,
  output REGDEST,
  output JUMP,
  output BRANCH,
  output MEMTOREG,
  output [2:0] ALUOP,
  output MEMWRITE,
  output ALUSRC,
  output REGWRITE,
  output BEQ,
  output BNE,
  output JAL,
  output LUI,
  output ANDI,
  output MOVE,
  output CLEAR,
  output LI
);

  UC uc_1 (
    .UC5(in_1[5]), .UC4(in_1[4]), .UC3(in_1[3]), .UC2(in_1[2]), .UC1(in_1[1]), .UC0(in_1[0]),
    .REGDEST(REGDEST), .JUMP(JUMP), .BRANCH(BRANCH), .MEMTOREG(MEMTOREG), .ULA0P1(ALUOP[1]),
    .ULA0P0(ALUOP[0]), .ULAOPSRC(ALUOP[2]), .MEM_WR(MEMWRITE), .ULASRC(ALUSRC), .WR(REGWRITE), .BEQ(BEQ),
    .BNE(BNE), .JAL(JAL), .LUI(LUI), .ANDI(ANDI), .MOVE(MOVE), .CLEAR(CLEAR), .LI(LI));
endmodule

module matrix_wr (
  input  [15:0] address,
  input  wr,
  input  clk,
  input  data,
  output [7:0] row0,
  output [7:0] row1,
  output [7:0] row2,
  output [7:0] row3,
  output [7:0] row4,
  output [7:0] row5,
  output [7:0] row6,
  output [7:0] row7
);

  wire t0, t1, t2, t3, t4, t5, t6, t7;

  Decoder #(.select(3), .disabled(0)) decoder_1 (
    .out0(t0), .out1(t1), .out2(t2), .out3(t3), .out4(t4), .out5(t5), .out6(t6), .out7(t7),
    .sel(address[5:3]), .en(wr));
  row row_1 (.data_in(data), .row_en(t0), .col(address[2:0]), .clk(clk), .out(row0));
  row row_2 (.data_in(data), .row_en(t1), .col(address[2:0]), .clk(clk), .out(row1));
  row row_3 (.data_in(data), .row_en(t2), .col(address[2:0]), .clk(clk), .out(row2));
  row row_4 (.data_in(data), .row_en(t3), .col(address[2:0]), .clk(clk), .out(row3));
  row row_5 (.data_in(data), .row_en(t4), .col(address[2:0]), .clk(clk), .out(row4));
  row row_6 (.data_in(data), .row_en(t5), .col(address[2:0]), .clk(clk), .out(row5));
  row row_7 (.data_in(data), .row_en(t6), .col(address[2:0]), .clk(clk), .out(row6));
  row row_8 (.data_in(data), .row_en(t7), .col(address[2:0]), .clk(clk), .out(row7));

  // Other names for the same wires on the sheet: col[2:0] = address[2:0]; data_in = data
endmodule

module row (
  input  data_in,
  input  row_en,
  input  [2:0] col,
  input  clk,
  output [7:0] out
);

  wire decoder_1_out0, decoder_1_out1, decoder_1_out2, decoder_1_out3, decoder_1_out4, decoder_1_out5,
       decoder_1_out6, decoder_1_out7;

  Decoder #(.select(3), .disabled(0)) decoder_1 (
    .out0(decoder_1_out0), .out1(decoder_1_out1), .out2(decoder_1_out2), .out3(decoder_1_out3),
    .out4(decoder_1_out4), .out5(decoder_1_out5), .out6(decoder_1_out6), .out7(decoder_1_out7), .sel(col),
    .en(row_en));
  Register #(.width(1), .Select("low")) register_1 (
    .D(data_in), .en(decoder_1_out0), .Q(out[0]), .clk(clk));  // open: clr
  Register #(.width(1), .Select("low")) register_2 (
    .D(data_in), .en(decoder_1_out1), .Q(out[1]), .clk(clk));  // open: clr
  Register #(.width(1), .Select("low")) register_3 (
    .D(data_in), .en(decoder_1_out2), .Q(out[2]), .clk(clk));  // open: clr
  Register #(.width(1), .Select("low")) register_4 (
    .D(data_in), .en(decoder_1_out3), .Q(out[3]), .clk(clk));  // open: clr
  Register #(.width(1), .Select("low")) register_5 (
    .D(data_in), .en(decoder_1_out4), .Q(out[4]), .clk(clk));  // open: clr
  Register #(.width(1), .Select("low")) register_6 (
    .D(data_in), .en(decoder_1_out5), .Q(out[5]), .clk(clk));  // open: clr
  Register #(.width(1), .Select("low")) register_7 (
    .D(data_in), .en(decoder_1_out6), .Q(out[6]), .clk(clk));  // open: clr
  Register #(.width(1), .Select("low")) register_8 (
    .D(data_in), .en(decoder_1_out7), .Q(out[7]), .clk(clk));  // open: clr
endmodule

module SYSTEM (
  input  [31:0] DATA_MEM,
  input  MEM_READ,
  input  [15:0] ADDRESS_IN,
  input  wr_mem,
  input  [31:0] DATA_WR,
  input  LEFT,
  input  DOWN,
  input  RIGHT,
  input  UP,
  input  CLK,
  output [15:0] out_11,
  output [15:0] out_12,
  output [15:0] out_13,
  output [15:0] out_14,
  output [31:0] DATA_OUT,
  output [15:0] out_16,
  output [15:0] out_17,
  output [15:0] out_18,
  output [15:0] out_19,
  output [15:0] out_20,
  output [15:0] out_21,
  output [15:0] out_22,
  output [15:0] out_23,
  output [15:0] out_24,
  output [15:0] out_25,
  output [15:0] out_26,
  output [15:0] out_27
);

  wire and_1_out, and_2_out, and_3_out, and_4_out, and_5_out, and_6_out, bit_extender_1_out, comparator_1_eq,
       comparator_2_eq, comparator_3_eq, comparator_4_eq, comparator_5_eq, comparator_6_eq, or_1_out,
       or_2_out, or_3_out, or_4_out;
  wire [3:0] d_ff_1_q, random_1_out;
  wire [31:0] bit_extender_2_out, bit_extender_3_out, keyboard, multiplexer_2_out;

  Comparator #(.width(16)) comparator_1 (.a(ADDRESS_IN), .b(16'hfefe), .eq(comparator_1_eq));  // open: gt, lt
  Multiplexer #(.width(32), .enable("false")) multiplexer_1 (
    .in0(multiplexer_2_out), .in1(bit_extender_2_out), .out(DATA_OUT), .sel(and_1_out));
  Random #(.width(4)) random_1 (.clk(CLK), .out(random_1_out));  // open: next, clr
  Bit_Extender #(.in_width(32), .out_width(1), .\type ("zero")) bit_extender_1 (.in(DATA_WR), .out(bit_extender_1_out));
  or or_1 (or_1_out, DOWN, RIGHT, UP);
  or or_2 (or_2_out, LEFT, RIGHT, UP);
  or or_3 (or_3_out, LEFT, DOWN, UP);
  or or_4 (or_4_out, LEFT, DOWN, RIGHT);
  Multiplexer #(.width(32), .enable("false")) multiplexer_2 (
    .in0(DATA_MEM), .in1(keyboard), .out(multiplexer_2_out), .sel(and_2_out));
  and and_1 (and_1_out, comparator_1_eq, MEM_READ);
  assign bit_extender_2_out = {{28{1'b0}}, random_1_out};  // Bit_Extender bit_extender_2
  D_Flip_Flop d_ff_1 (.Q(d_ff_1_q[0]), .preset(LEFT), .reset(or_1_out));  // open: clk, D, Qn
  D_Flip_Flop d_ff_2 (.Q(d_ff_1_q[1]), .preset(DOWN), .reset(or_2_out));  // open: clk, D, Qn
  D_Flip_Flop d_ff_3 (.Q(d_ff_1_q[2]), .preset(RIGHT), .reset(or_3_out));  // open: clk, D, Qn
  D_Flip_Flop d_ff_4 (.Q(d_ff_1_q[3]), .preset(UP), .reset(or_4_out));  // open: clk, D, Qn
  and and_2 (and_2_out, MEM_READ, comparator_2_eq);
  Comparator #(.width(16)) comparator_2 (.a(16'hfeff), .b(ADDRESS_IN), .eq(comparator_2_eq));  // open: gt, lt
  assign bit_extender_3_out = {{28{1'b0}}, d_ff_1_q};  // Bit_Extender bit_extender_3
  Register #(.width(32), .Select("low")) register_1 (.D(bit_extender_3_out), .Q(keyboard), .clk(CLK));  // open: en, clr
  Comparator #(.width(10)) comparator_3 (.a(ADDRESS_IN[15:6]), .b(10'h3fc), .eq(comparator_3_eq));  // open: gt, lt
  Comparator #(.width(10)) comparator_4 (.a(ADDRESS_IN[15:6]), .b(10'h3fd), .eq(comparator_4_eq));  // open: gt, lt
  Comparator #(.width(10)) comparator_5 (.a(ADDRESS_IN[15:6]), .b(10'h3fe), .eq(comparator_5_eq));  // open: gt, lt
  Comparator #(.width(10)) comparator_6 (.a(ADDRESS_IN[15:6]), .b({10{1'b1}}), .eq(comparator_6_eq));  // open: gt, lt
  and and_3 (and_3_out, wr_mem, comparator_3_eq);
  and and_4 (and_4_out, wr_mem, comparator_4_eq);
  and and_5 (and_5_out, wr_mem, comparator_5_eq);
  and and_6 (and_6_out, wr_mem, comparator_6_eq);
  matrix_wr matrix_wr_1 (
    .address(ADDRESS_IN), .wr(and_3_out), .clk(CLK), .data(bit_extender_1_out), .row0(out_11[7:0]),
    .row1(out_11[15:8]), .row2(out_12[7:0]), .row3(out_12[15:8]), .row4(out_13[7:0]), .row5(out_13[15:8]),
    .row6(out_14[7:0]), .row7(out_14[15:8]));
  matrix_wr matrix_wr_2 (
    .address(ADDRESS_IN), .wr(and_4_out), .clk(CLK), .data(bit_extender_1_out), .row0(out_16[7:0]),
    .row1(out_16[15:8]), .row2(out_17[7:0]), .row3(out_17[15:8]), .row4(out_18[7:0]), .row5(out_18[15:8]),
    .row6(out_19[7:0]), .row7(out_19[15:8]));
  matrix_wr matrix_wr_3 (
    .address(ADDRESS_IN), .wr(and_5_out), .clk(CLK), .data(bit_extender_1_out), .row0(out_20[7:0]),
    .row1(out_20[15:8]), .row2(out_21[7:0]), .row3(out_21[15:8]), .row4(out_22[7:0]), .row5(out_22[15:8]),
    .row6(out_23[7:0]), .row7(out_23[15:8]));
  matrix_wr matrix_wr_4 (
    .address(ADDRESS_IN), .wr(and_6_out), .clk(CLK), .data(bit_extender_1_out), .row0(out_24[7:0]),
    .row1(out_24[15:8]), .row2(out_25[7:0]), .row3(out_25[15:8]), .row4(out_26[7:0]), .row5(out_26[15:8]),
    .row6(out_27[7:0]), .row7(out_27[15:8]));
endmodule

module BEQ_BNE (
  input  BRANCH,
  input  BEQ,
  input  BNE,
  input  in_4,
  output out_5
);

  wire multiplexer_1_out, multiplexer_2_out, not_1_out, or_1_out;

  or or_1 (or_1_out, BEQ, BNE);
  and and_1 (out_5, BRANCH, multiplexer_1_out);
  Multiplexer #(.enable("false")) multiplexer_1 (
    .in0(1'b0), .in1(multiplexer_2_out), .out(multiplexer_1_out), .sel(or_1_out));
  Multiplexer #(.enable("false")) multiplexer_2 (.in0(not_1_out), .in1(in_4), .out(multiplexer_2_out), .sel(BEQ));
  not not_1 (not_1_out, in_4);
endmodule

module MUX_S (
  input  JUMP,
  input  BEQ_BNE,
  input  JAL,
  input  JR,
  input  [31:0] PC___4,
  input  [31:0] IMEDIATO_EXT,
  input  [31:0] RD,
  output [31:0] out_8
);

  wire [31:0] adder_1_out, multiplexer_1_out, multiplexer_2_out, multiplexer_3_out, shifter_1_out;

  Multiplexer #(.width(32), .enable("false")) multiplexer_1 (
    .in0(PC___4), .in1({PC___4[31:28], IMEDIATO_EXT[27:2], 2'b00}), .out(multiplexer_1_out), .sel(JUMP));
  Shifter #(.width(32)) shifter_1 (.in(IMEDIATO_EXT), .\dist (5'b00010), .out(shifter_1_out));
  Multiplexer #(.width(32), .enable("false")) multiplexer_2 (
    .in0(multiplexer_1_out), .in1(adder_1_out), .out(multiplexer_2_out), .sel(BEQ_BNE));
  Adder #(.width(32)) adder_1 (.a(PC___4), .b(shifter_1_out), .out(adder_1_out));  // open: cin, cout
  Multiplexer #(.width(32), .enable("false")) multiplexer_3 (
    .in0(multiplexer_2_out), .in1({PC___4[31:28], IMEDIATO_EXT[27:2], 2'b00}), .out(multiplexer_3_out),
    .sel(JAL));
  Multiplexer #(.width(32), .enable("false")) multiplexer_4 (.in0(multiplexer_3_out), .in1(RD), .out(out_8), .sel(JR));
endmodule

module atlas_extensor (
  input  [15:0] in_1,
  output [31:0] out_2,
  output [31:0] out_3
);

  assign out_2 = {{16{1'b0}}, in_1};  // Bit_Extender bit_extender_1
  assign out_3 = {{16{in_1[15]}}, in_1};  // Bit_Extender bit_extender_2
endmodule
